// Logisim project Logisim-212-221.circ as structural Verilog: 8 circuits, main circuit main
module main (
  input  r0,
  input  r1,
  input  r2,
  input  r3,
  input  r4,
  input  r5,
  input  r6,
  input  r7,
  input  Enable,
  input  Clear,
  output Q0,
  output Q1,
  output Q2,
  output Q3,
  output Q4,
  output Q5,
  output Q6,
  output Q7,
  output [2:0] out_19
);

  wire ANY_R_out, Clock_out, ic_7447_1_out_7, ic_7447_1_out_8, ic_7447_1_out_9, ic_7447_1_out_10,
       ic_7447_1_out_11, ic_7447_1_out_12, ic_7447_1_out_13, multiplexer_3_out;
  wire [2:0] adder_1_out, index_service_1_out_11, index_service_1_out_12, index_service_1_out_13,
       index_service_1_out_14, index_service_1_out_15, index_service_1_out_16, index_service_1_out_17,
       index_service_1_out_18, multiplexer_1_out, register_1_q;

  Clock Clock (.out(Clock_out));
  Adder #(.width(3)) adder_1 (.a(3'b001), .b(register_1_q), .out(adder_1_out));  // open: cin, cout
  Index_Service index_service_1 (
    .Enable(Enable), .in_1(r7), .in_2(r6), .in_3(r5), .in_4(r4), .in_5(r3), .in_6(r2), .in_7(r1), .in_8(r0),
    .out_11(index_service_1_out_11), .out_12(index_service_1_out_12), .out_13(index_service_1_out_13),
    .out_14(index_service_1_out_14), .out_15(index_service_1_out_15), .out_16(index_service_1_out_16),
    .out_17(index_service_1_out_17), .out_18(index_service_1_out_18), .Any_r(ANY_R_out));
  Multiplexer #(.select(3), .width(3), .enable("false")) multiplexer_1 (
    .in0(index_service_1_out_11), .in1(index_service_1_out_12), .in2(index_service_1_out_13),
    .in3(index_service_1_out_14), .in4(index_service_1_out_15), .in5(index_service_1_out_16),
    .in6(index_service_1_out_17), .in7(index_service_1_out_18), .out(multiplexer_1_out), .sel(adder_1_out));
  Multiplexer #(.width(3)) multiplexer_2 (
    .in0(register_1_q), .in1(multiplexer_1_out), .out(out_19), .sel(ANY_R_out), .en(Enable));
  Register_part #(.width(3)) register_1 (.D(out_19), .en(Enable), .Q(register_1_q), .clk(Clock_out), .clr(Clear));
  or ANY_R (ANY_R_out, r0, r1, r2, r3, r4, r5, r6, r7);
  Grant_Service grant_service_1 (
    .in_2(out_19), .Any_Request(ANY_R_out), .Q0(Q0), .Q1(Q1), .Q2(Q2), .Q3(Q3), .Q4(Q4), .Q5(Q5), .Q6(Q6),
    .Q7(Q7));
  Multiplexer #(.enable("false")) multiplexer_3 (.in0(1'b0), .in1(1'b1), .out(multiplexer_3_out), .sel(ANY_R_out));
  IC_7447 ic_7447_1 (
    .in_1(out_19[0]), .in_2(out_19[1]), .in_3(out_19[2]), .in_4(1'b0), .in_5(multiplexer_3_out),
    .in_6(multiplexer_3_out), .out_7(ic_7447_1_out_7), .out_8(ic_7447_1_out_8), .out_9(ic_7447_1_out_9),
    .out_10(ic_7447_1_out_10), .out_11(ic_7447_1_out_11), .out_12(ic_7447_1_out_12), .out_13(ic_7447_1_out_13));
  _7_Segment_Display u_7_segment_display_1 (
    .g(ic_7447_1_out_13), .f(ic_7447_1_out_12), .a(ic_7447_1_out_7), .b(ic_7447_1_out_8),
    .e(ic_7447_1_out_11), .d(ic_7447_1_out_10), .c(ic_7447_1_out_9));  // open: dp

  // Notes on the sheet:
  //   INPUT SIDE
  //   REQUESTS
  //   WEIGHTED (INDEX BASED)
  //   Increment by 1
  //   ROUND ROBIN ARBITER
  //   The Arbiter goes back to the first served request when all the requests have been granted once.
  //   Index Service
  //   Designed by Govind Jeevan and Bidyadhar Mohanty
  //   If the weight of a port is 0, then the arbiter while moving in Round Robin fashion, skips that port to serve the next port with wieight 1.
  //   When there are multiple requests for the same resource, the round robin arbiter allocates the resource for each of the requests for a specific period of time, in order.
  //   3 Bit Register
  //   Grant Service
  //   Power
  //   IC7447
  //   GRANTED ID
  //   BCD to Seven Segment Decoder
  //   OUTPUT SIDE
  //   GRANTS
endmodule

module _2_1_MUX (
  input  Select_Line,
  input  input_1,
  input  Input_2,
  output Output
);

  wire and_1_out, and_2_out, not_1_out;

  not not_1 (not_1_out, Select_Line);
  and and_1 (and_1_out, not_1_out, input_1);
  and and_2 (and_2_out, Select_Line, Input_2);
  or or_1 (Output, and_1_out, and_2_out);

  // Notes on the sheet:
  //   2-1 MUX
endmodule

module _3_8_Decoder (
  input  in_1,
  input  in_2,
  input  in_3,
  output out_4,
  output out_5,
  output out_6,
  output out_7,
  output out_8,
  output out_9,
  output out_10,
  output out_11
);

  wire not_1_out, not_2_out, not_3_out;

  not not_1 (not_1_out, in_1);
  not not_2 (not_2_out, in_2);
  not not_3 (not_3_out, in_3);
  and and_1 (out_4, not_3_out, not_2_out, not_1_out);
  and and_2 (out_5, in_3, not_2_out, not_1_out);
  and and_3 (out_6, not_1_out, in_2, not_3_out);
  and and_4 (out_7, in_3, in_2, not_1_out);
  and and_5 (out_8, not_3_out, not_2_out, in_1);
  and and_6 (out_9, in_3, not_2_out, in_1);
  and and_7 (out_10, not_1_out, in_2, in_1);
  and and_8 (out_11, in_3, in_2, in_1);

  // Notes on the sheet:
  //   Inputs
  //   3-8 Decoder
  //   Outputs
endmodule

module Register (
  input  [2:0] _3_Bit_Input,
  input  Clear,
  input  Enable,
  input  Preset,
  output [2:0] _3_Bit_Output
);

  wire Clock_out;

  Clock Clock (.out(Clock_out));
  D_Flip_Flop d_ff_1 (
    .clk(Clock_out), .D(_3_Bit_Input[2]), .Q(_3_Bit_Output[2]), .preset(Preset), .en(Enable), .reset(Clear));  // open: Qn
  D_Flip_Flop d_ff_2 (
    .clk(Clock_out), .D(_3_Bit_Input[1]), .Q(_3_Bit_Output[1]), .preset(Preset), .en(Enable), .reset(Clear));  // open: Qn
  D_Flip_Flop d_ff_3 (
    .clk(Clock_out), .D(_3_Bit_Input[0]), .Q(_3_Bit_Output[0]), .preset(Preset), .en(Enable), .reset(Clear));  // open: Qn

  // Notes on the sheet:
  //   Register
  //   3- Bit Parallel In Parallel Out
endmodule

module IC_7447 (
  input  in_1,
  input  in_2,
  input  in_3,
  input  in_4,
  input  in_5,
  input  in_6,
  output out_7,
  output out_8,
  output out_9,
  output out_10,
  output out_11,
  output out_12,
  output out_13
);

  wire and_1_out, and_2_out, and_3_out, and_4_out, and_5_out, and_6_out, and_7_out, and_8_out, and_9_out,
       and_10_out, and_11_out, and_12_out, and_13_out, and_14_out, and_15_out, and_16_out, and_17_out,
       buffer_1_out, buffer_2_out, buffer_3_out, nand_1_out, nand_2_out, nand_3_out, nand_4_out, nand_5_out,
       nand_6_out, nand_7_out, nand_8_out, not_1_out, not_2_out;

  not not_1 (not_1_out, in_4);
  buf buffer_1 (buffer_1_out, in_5);
  not not_2 (not_2_out, in_6);
  nand nand_1 (nand_1_out, in_1, buffer_1_out);
  nand nand_2 (nand_2_out, in_2, buffer_1_out);
  nand nand_3 (nand_3_out, in_3, buffer_1_out);
  nand nand_4 (nand_4_out, nand_1_out, buffer_2_out);
  nand nand_5 (nand_5_out, nand_2_out, buffer_2_out);
  nand nand_6 (nand_6_out, nand_3_out, buffer_2_out);
  nand nand_7 (nand_7_out, not_1_out, buffer_2_out);
  nand nand_8 (nand_8_out, buffer_1_out, not_2_out, not_1_out, nand_2_out, nand_1_out);
  buf buffer_2 (buffer_2_out, nand_8_out);
  and and_1 (and_1_out, nand_5_out, nand_7_out);
  and and_2 (and_2_out, nand_1_out, nand_6_out);
  and and_3 (and_3_out, nand_5_out, nand_7_out);
  and and_4 (and_4_out, nand_4_out, nand_2_out, nand_6_out);
  and and_5 (and_5_out, nand_1_out, nand_5_out, nand_6_out);
  and and_6 (and_6_out, nand_6_out, nand_7_out);
  and and_7 (and_7_out, nand_1_out, nand_5_out, nand_3_out);
  and and_8 (and_8_out, nand_4_out, nand_2_out, nand_3_out);
  and and_9 (and_9_out, nand_1_out, nand_2_out, nand_6_out);
  and and_10 (and_10_out, nand_4_out, nand_5_out, nand_6_out);
  buf buffer_3 (buffer_3_out, nand_4_out);
  and and_11 (and_11_out, nand_2_out, nand_6_out);
  and and_12 (and_12_out, nand_4_out, nand_5_out);
  and and_13 (and_13_out, nand_5_out, nand_3_out);
  and and_14 (and_14_out, nand_4_out, not_1_out, nand_3_out);
  and and_15 (and_15_out, nand_4_out, nand_5_out, nand_6_out);
  and and_16 (and_16_out, nand_4_out, nand_2_out, nand_3_out, not_1_out);
  and and_17 (and_17_out, nand_2_out, nand_3_out, not_1_out, buffer_1_out);
  nor nor_1 (out_7, and_1_out, and_2_out, and_16_out);
  nor nor_2 (out_8, and_3_out, and_4_out, and_5_out);
  nor nor_3 (out_9, and_6_out, and_7_out);
  nor nor_4 (out_10, and_8_out, and_9_out, and_10_out);
  nor nor_5 (out_11, buffer_3_out, and_11_out);
  nor nor_6 (out_12, and_12_out, and_13_out, and_14_out);
  nor nor_7 (out_13, and_15_out, and_17_out);

  // Notes on the sheet:
  //   IC 7447
endmodule

module Grant_Service (
  input  Any_Request,
  input  [2:0] in_2,
  output Q0,
  output Q1,
  output Q2,
  output Q3,
  output Q4,
  output Q5,
  output Q6,
  output Q7
);

  wire decoder_1_out0, decoder_1_out1, decoder_1_out2, decoder_1_out3, decoder_1_out4, decoder_1_out5,
       decoder_1_out6, decoder_1_out7;

  Decoder #(.select(3), .enable("false")) decoder_1 (
    .out0(decoder_1_out0), .out1(decoder_1_out1), .out2(decoder_1_out2), .out3(decoder_1_out3),
    .out4(decoder_1_out4), .out5(decoder_1_out5), .out6(decoder_1_out6), .out7(decoder_1_out7), .sel(in_2));
  and and_1 (Q0, Any_Request, decoder_1_out0);
  and and_2 (Q1, Any_Request, Any_Request, Any_Request, decoder_1_out1);
  and and_3 (Q2, decoder_1_out2, decoder_1_out2, decoder_1_out2, Any_Request);
  and and_4 (Q3, Any_Request, Any_Request, Any_Request, decoder_1_out3);
  and and_5 (Q4, Any_Request, Any_Request, Any_Request, decoder_1_out4);
  and and_6 (Q5, Any_Request, Any_Request, Any_Request, decoder_1_out5);
  and and_7 (Q6, decoder_1_out6, decoder_1_out6, decoder_1_out6, Any_Request);
  and and_8 (Q7, decoder_1_out7, decoder_1_out7, decoder_1_out7, Any_Request);

  // Notes on the sheet:
  //   Granted Request
  //   Grant Service
endmodule

module Index_Service (
  input  in_1,
  input  in_2,
  input  in_3,
  input  in_4,
  input  in_5,
  input  in_6,
  input  in_7,
  input  in_8,
  input  Any_r,
  input  Enable,
  output [2:0] out_11,
  output [2:0] out_12,
  output [2:0] out_13,
  output [2:0] out_14,
  output [2:0] out_15,
  output [2:0] out_16,
  output [2:0] out_17,
  output [2:0] out_18
);

  wire nand_1_out, nand_2_out, nand_3_out, nand_4_out, nand_5_out, nand_6_out, nand_7_out, nand_8_out,
       not_1_out, not_2_out, not_3_out, not_4_out, not_5_out, not_6_out, not_7_out, not_8_out;

  not not_1 (not_1_out, in_1);
  nand nand_1 (nand_1_out, not_1_out, Any_r);
  Multiplexer #(.width(3)) multiplexer_1 (.in0(out_11), .in1(3'b111), .out(out_18), .sel(nand_1_out), .en(Enable));
  not not_2 (not_2_out, in_2);
  nand nand_2 (nand_2_out, not_2_out, Any_r);
  not not_3 (not_3_out, in_3);
  Multiplexer #(.width(3)) multiplexer_2 (.in0(out_18), .in1(3'b110), .out(out_17), .sel(nand_2_out), .en(Enable));
  not not_4 (not_4_out, in_4);
  nand nand_3 (nand_3_out, not_3_out, Any_r);
  Multiplexer #(.width(3)) multiplexer_3 (.in0(out_17), .in1(3'b101), .out(out_16), .sel(nand_3_out), .en(Enable));
  nand nand_4 (nand_4_out, not_4_out, Any_r);
  Multiplexer #(.width(3)) multiplexer_4 (.in0(out_16), .in1(3'b100), .out(out_15), .sel(nand_4_out), .en(Enable));
  not not_5 (not_5_out, in_5);
  nand nand_5 (nand_5_out, not_5_out, Any_r);
  Multiplexer #(.width(3)) multiplexer_5 (.in0(out_15), .in1(3'b011), .out(out_14), .sel(nand_5_out), .en(Enable));
  not not_6 (not_6_out, in_6);
  nand nand_6 (nand_6_out, not_6_out, Any_r);
  Multiplexer #(.width(3)) multiplexer_6 (.in0(out_14), .in1(3'b010), .out(out_13), .sel(nand_6_out), .en(Enable));
  not not_7 (not_7_out, in_7);
  nand nand_7 (nand_7_out, not_7_out, Any_r);
  not not_8 (not_8_out, in_8);
  nand nand_8 (nand_8_out, not_8_out, Any_r);
  Multiplexer #(.width(3)) multiplexer_7 (.in0(out_13), .in1(3'b001), .out(out_12), .sel(nand_7_out), .en(Enable));
  Multiplexer #(.width(3)) multiplexer_8 (.in0(out_12), .in1(3'b000), .out(out_11), .sel(nand_8_out), .en(Enable));

  // Notes on the sheet:
  //   Weights ->
  //   Requests
  //   Index Service
endmodule

module _8_1_MUX (
  input  S0,
  input  S1,
  input  S2,
  input  I0,
  input  I1,
  input  I2,
  input  I3,
  input  I4,
  input  I5,
  input  I6,
  input  I7,
  output out_12
);

  wire n2_1_mux_1_output, n2_1_mux_2_output, n2_1_mux_3_output, n2_1_mux_4_output, n2_1_mux_5_output,
       n2_1_mux_6_output;

  _2_1_MUX u_2_1_mux_1 (.input_1(I0), .Input_2(I1), .Select_Line(S0), .Output(n2_1_mux_1_output));
  _2_1_MUX u_2_1_mux_2 (.input_1(I2), .Input_2(I3), .Select_Line(S0), .Output(n2_1_mux_2_output));
  _2_1_MUX u_2_1_mux_3 (.input_1(I4), .Input_2(I5), .Select_Line(S0), .Output(n2_1_mux_3_output));
  _2_1_MUX u_2_1_mux_4 (.input_1(I6), .Input_2(I7), .Select_Line(S0), .Output(n2_1_mux_4_output));
  _2_1_MUX u_2_1_mux_5 (
    .input_1(n2_1_mux_1_output), .Input_2(n2_1_mux_2_output), .Select_Line(S1), .Output(n2_1_mux_5_output));
  _2_1_MUX u_2_1_mux_6 (
    .input_1(n2_1_mux_3_output), .Input_2(n2_1_mux_4_output), .Select_Line(S1), .Output(n2_1_mux_6_output));
  _2_1_MUX u_2_1_mux_7 (.input_1(n2_1_mux_5_output), .Input_2(n2_1_mux_6_output), .Select_Line(S2), .Output(out_12));

  // Notes on the sheet:
  //   8-1 MUX
  //   Using 2-1 MUX
endmodule
